// Digital circuit alu.dig as structural Verilog
module alu (
  input  [4:0] op,
  input  [15:0] X,
  input  [15:0] Y,
  output [15:0] Z,
  output [15:0] rem,
  output ov
);

  wire add_1_c_o, compare_1_p4, sub_1_c_o;
  wire [15:0] add_1_s, and_1_out, barrelshifter_1_out, barrelshifter_2_out, div_1_q, nand_1_out, nor_1_out,
       not_1_out, not_2_out, or_1_out, out_arithmetic, out_compare, out_logic, sub_1_s, xnor_1_out, xor_1_out;
  wire [31:0] mul_1_mul;

  Multiplexer #(.Selector_Bits(2), .Bits(16)) multiplexer_1 (
    .sel(op[4:3]), .in_0(out_arithmetic), .in_1({16{1'b0}}), .in_2(out_logic), .in_3(out_compare), .out(Z));
  // compare compare_1: pin names not known; wires that end beside it: op[2:0], X, Y, compare_1_p4
  Add #(.Bits(16)) add_1 (.a(X), .b(Y), .c_i(1'b0), .s(add_1_s), .c_o(add_1_c_o));
  Sub #(.Bits(16)) sub_1 (.a(X), .b(Y), .c_i(1'b0), .s(sub_1_s), .c_o(sub_1_c_o));
  Mul #(.Signed("true"), .Bits(16)) mul_1 (.a(X), .b(Y), .mul(mul_1_mul));
  Div #(.Signed("true"), .Bits(16)) div_1 (.a(X), .b(Y), .q(div_1_q), .r(rem));
  BarrelShifter #(.Bits(16), .barrelSigned("true"), .direction("right")) barrelshifter_1 (
    .in(X), .shift(Y[5:0]), .out(barrelshifter_1_out));
  BarrelShifter #(.Bits(16), .barrelSigned("true")) barrelshifter_2 (.in(X), .shift(Y[5:0]), .out(barrelshifter_2_out));
  assign and_1_out = X & Y;  // And and_1, 16 bits wide
  assign or_1_out = X | Y;  // Or or_1, 16 bits wide
  assign not_1_out = ~X;  // Not not_1, 16 bits wide
  assign not_2_out = ~Y;  // Not not_2, 16 bits wide
  assign xor_1_out = X ^ Y;  // XOr xor_1, 16 bits wide
  assign xnor_1_out = ~(X ^ Y);  // XNOr xnor_1, 16 bits wide
  assign nor_1_out = ~(X | Y);  // NOr nor_1, 16 bits wide
  assign nand_1_out = ~(X & Y);  // NAnd nand_1, 16 bits wide
  or or_2 (ov, add_1_c_o, sub_1_c_o);
  Multiplexer #(.Bits(16)) multiplexer_2 (.sel(compare_1_p4), .in_0({16{1'b0}}), .in_1({16{1'b1}}), .out(out_compare));
  Multiplexer #(.Selector_Bits(3), .Bits(16)) multiplexer_3 (
    .sel(op[2:0]), .in_0(add_1_s), .in_1(sub_1_s), .in_2(mul_1_mul[15:0]), .in_3(div_1_q),
    .in_4(barrelshifter_1_out), .in_5(barrelshifter_2_out), .in_6({16{1'b0}}), .in_7({16{1'b0}}),
    .out(out_arithmetic));
  Multiplexer #(.Selector_Bits(3), .Bits(16)) multiplexer_4 (
    .sel(op[2:0]), .in_0(and_1_out), .in_1(or_1_out), .in_2(not_1_out), .in_3(not_2_out), .in_4(xor_1_out),
    .in_5(xnor_1_out), .in_6(nor_1_out), .in_7(nand_1_out), .out(out_logic));

  // Other names for the same wires on the sheet: op_t[2:0] = op[2:0]; section[1:0] = op[4:3]

  // Notes on the sheet:
  //   input
  //   output
  //   arithmetic
  //   logic
  //   comparison
endmodule

/* Test case procedural tests:
  opcode  X   Y   Z

loop(i,50)
  let x = random(0xFFFF);
  let y = random(0xFFFF);

  0b00000 (x) (y) (x+y) 
  0b00001 (x) (y) (x-y)
  0b00010 (x) (y) (x*y)
# division often fails because digital does not use signed division
#  0b00011 (x) (y) (x/y)
# shifting done separately with lower X

  0b10000 (x) (y) (x&y)
  0b10001 (x) (y) (x|y)
  0b10010 (x) (y) (~x)
# 0b10011
  0b10100 (x) (y) (x^y)
  0b10101 (x) (y) (~(x^y))
  0b10110 (x) (y) (~(x|y))
  0b10111 (x) (y) (~(x&y))

# comparison often fails because digital does not do signed comparisons
  0b11000 (x) (y) 0x0000
#  0b11001 (x) (y) (ite(x> y, 0xFFFF, 0x0000))
#  0b11010 (x) (y) (ite(x= y, 0xFFFF, 0x0000))
#  0b11011 (x) (y) (ite(x>=y, 0xFFFF, 0x0000))
#  0b11100 (x) (y) (ite(x< y, 0xFFFF, 0x0000))
#  0b11101 (x) (y) (ite(x!=y, 0xFFFF, 0x0000))
#  0b11110 (x) (y) (ite(x<=y, 0xFFFF, 0x0000))
  0b11111 (x) (y) 0xFFFF
end loop


loop(j,50)
  let x = random(0xFFFF);
  let y = random(16);

  0b00100 (x) (y) (x>>y)
  0b00101 (x) (y) (x<<y)
end loop
*/

/* Test case arithmetic:
opcode      X       Y       Z    remainder
# addition
0b00000  0x0000  0x0000  0x0000  x
0b00000  0x0001  0x0000  0x0001  x
0b00000  0x0000  0x0001  0x0001  x
0b00000  0x0001  0x0001  0x0002  x
0b00000  0x0002  0x0003  0x0005  x

# subtraction
0b00001  0x0000  0x0000  0x0000  x
0b00001  0x0001  0x0000  0x0001  x
0b00001  0x0001  0x0001  0x0000  x
0b00001  0x0002  0x0001  0x0001  x
0b00001  0x0002  0x0000  0x0002  x
0b00001  0x0001  0x0002  0xFFFF  x
0b00001  0x0000  0x0001  0xFFFF  x
0b00001  0x0000  0x0002  0xFFFE  x

# multiplication
0b00010  0x0000  0x0000  0x0000  x
0b00010  0x0001  0x0000  0x0000  x
0b00010  0x0000  0x0001  0x0000  x
0b00010  0x0001  0x0001  0x0001  x
0b00010  0x0000  0x0002  0x0000  x
0b00010  0x0002  0x0000  0x0000  x
0b00010  0x0002  0x0002  0x0004  x
0b00010  0x0002  0x0001  0x0002  x
0b00010  0x0001  0x0002  0x0002  x
0b00010  0xFFFF  0x0002  0xFFFE  x
0b00010  0x0002  0xFFFF  0xFFFE  x

# division
0b00011  0x0001  0x0001  0x0001  0
0b00011  0x0002  0x0001  0x0002  0
0b00011  0x0003  0x0001  0x0003  0
0b00011  0x0004  0x0001  0x0004  0
0b00011  0x0005  0x0001  0x0005  0
0b00011  0x0006  0x0001  0x0006  0
0b00011  0x0007  0x0001  0x0007  0

0b00011  0x0001  0x0002  0x0000  1
0b00011  0x0002  0x0002  0x0001  0
0b00011  0x0003  0x0002  0x0001  1
0b00011  0x0004  0x0002  0x0002  0
0b00011  0x0005  0x0002  0x0002  1
0b00011  0x0006  0x0002  0x0003  0
0b00011  0x0007  0x0002  0x0003  1

# shift right
0b00100  0x0000  0x0000  0x0000  x
0b00100  0x0000  0x0001  0x0000  x
0b00100  0x0000  0x0002  0x0000  x
0b00100  0x0002  0x0000  0x0002  x
0b00100  0x0002  0x0001  0x0001  x
0b00100  0x0002  0x0002  0x0000  x
0b00100  0x0003  0x0000  0x0003  x
0b00100  0x0003  0x0001  0x0001  x
0b00100  0x0003  0x0002  0x0000  x
0b00100  0x0004  0x0000  0x0004  x
0b00100  0x0004  0x0001  0x0002  x
0b00100  0x0004  0x0002  0x0001  x

# shift left
0b00101  0x0000  0x0000  0x0000  x
0b00101  0x0000  0x0001  0x0000  x
0b00101  0x0000  0x0002  0x0000  x
0b00101  0x0001  0x0000  0x0001  x
0b00101  0x0001  0x0001  0x0002  x
0b00101  0x0001  0x0002  0x0004  x
0b00101  0x0002  0x0000  0x0002  x
0b00101  0x0002  0x0001  0x0004  x
0b00101  0x0002  0x0002  0x0008  x
0b00101  0x0003  0x0000  0x0003  x
0b00101  0x0003  0x0001  0x0006  x
0b00101  0x0003  0x0002  0x000C  x
*/

/* Test case bitwise:
opcode   X       Y       Z
# bitwise and
0b10000  0x0000  0x0000  0x0000
0b10000  0x0000  0x0001  0x0000
0b10000  0x0001  0x0000  0x0000
0b10000  0x0001  0x0001  0x0001
0b10000  0x0002  0x0001  0x0000
0b10000  0x0001  0x0002  0x0000
0b10000  0x0002  0x0002  0x0002
0b10000  0x0002  0x0000  0x0000
0b10000  0x0000  0x0002  0x0000
0b10000  0x0003  0x0002  0x0002

# bitwise or
0b10001  0x0000  0x0000  0x0000
0b10001  0x0000  0x0001  0x0001
0b10001  0x0001  0x0000  0x0001
0b10001  0x0001  0x0001  0x0001
0b10001  0x0002  0x0001  0x0003
0b10001  0x0001  0x0002  0x0003
0b10001  0x0002  0x0002  0x0002
0b10001  0x0002  0x0000  0x0002
0b10001  0x0000  0x0002  0x0002
0b10001  0x0003  0x0002  0x0003

# bitwise not x
0b10010  0x0000  0x0000  0xFFFF
0b10010  0x0000  0x0001  0xFFFF
0b10010  0x0001  0x0000  0xFFFE
0b10010  0x0001  0x0001  0xFFFE
0b10010  0x0002  0x0000  0xFFFD
0b10010  0x0002  0x0001  0xFFFD
0b10010  0x0003  0x0000  0xFFFC
0b10010  0x0003  0x0001  0xFFFC
0b10010  0x0004  0x0000  0xFFFB
0b10010  0x0004  0x0001  0xFFFB

# bitwise not y
0b10011  0x0000  0x0000  0xFFFF
0b10011  0x0001  0x0000  0xFFFF
0b10011  0x0000  0x0001  0xFFFE
0b10011  0x0001  0x0001  0xFFFE
0b10011  0x0000  0x0002  0xFFFD
0b10011  0x0001  0x0002  0xFFFD
0b10011  0x0000  0x0003  0xFFFC
0b10011  0x0001  0x0003  0xFFFC
0b10011  0x0000  0x0004  0xFFFB
0b10011  0x0001  0x0004  0xFFFB

# bitwise xor
0b10100  0x0000  0x0000  0x0000
0b10100  0x0001  0x0000  0x0001
0b10100  0x0000  0x0001  0x0001
0b10100  0x0001  0x0001  0x0000
0b10100  0x0000  0x0002  0x0002
0b10100  0x0001  0x0002  0x0003
0b10100  0x0000  0x0003  0x0003
0b10100  0x0001  0x0003  0x0002
0b10100  0x0000  0x0004  0x0004

# bitwise xnor
0b10101  0x0000  0x0000  0xFFFF
0b10101  0x0001  0x0000  0xFFFE
0b10101  0x0000  0x0001  0xFFFE
0b10101  0x0001  0x0001  0xFFFF
0b10101  0x0000  0x0002  0xFFFD
0b10101  0x0001  0x0002  0xFFFC
0b10101  0x0000  0x0003  0xFFFC
0b10101  0x0001  0x0003  0xFFFD
0b10101  0x0000  0x0004  0xFFFB

# bitwise nor
0b10110  0x0000  0x0000  0xFFFF
0b10110  0x0001  0x0000  0xFFFE
0b10110  0x0000  0x0001  0xFFFE
0b10110  0x0001  0x0001  0xFFFE
0b10110  0x0000  0x0002  0xFFFD
0b10110  0x0001  0x0002  0xFFFC
0b10110  0x0000  0x0003  0xFFFC
0b10110  0x0001  0x0003  0xFFFC
0b10110  0x0000  0x0004  0xFFFB

# bitwise nand
0b10111  0x0000  0x0000  0xFFFF
0b10111  0x0001  0x0000  0xFFFF
0b10111  0x0000  0x0001  0xFFFF
0b10111  0x0001  0x0001  0xFFFE
0b10111  0x0000  0x0002  0xFFFF
0b10111  0x0001  0x0002  0xFFFF
0b10111  0x0000  0x0003  0xFFFF
0b10111  0x0001  0x0003  0xFFFE
0b10111  0x0000  0x0004  0xFFFF
*/

/* Test case comparison:
opcode   X       Y       Z
# false
0b11000  0x0000  0x0000  0x0000
0b11000  0x0000  0x0001  0x0000
0b11000  0x0001  0x0000  0x0000
0b11000  0x0001  0x0001  0x0000
0b11000  0x0002  0x0001  0x0000
0b11000  0x0001  0x0002  0x0000
0b11000  0x0002  0x0002  0x0000
0b11000  0x0002  0x0000  0x0000
0b11000  0x0000  0x0002  0x0000
0b11000  0x0003  0x0002  0x0000

# greater than
0b11001  0x0000  0x0000  0x0000
0b11001  0x0000  0x0001  0x0000
0b11001  0x0001  0x0000  0xFFFF
0b11001  0x0001  0x0001  0x0000
0b11001  0x0002  0x0001  0xFFFF
0b11001  0x0001  0x0002  0x0000
0b11001  0x0002  0x0002  0x0000
0b11001  0x0002  0x0000  0xFFFF
0b11001  0x0000  0x0002  0x0000
0b11001  0x0003  0x0002  0xFFFF

# equals
0b11010  0x0000  0x0000  0xFFFF
0b11010  0x0000  0x0001  0x0000
0b11010  0x0001  0x0000  0x0000
0b11010  0x0001  0x0001  0xFFFF
0b11010  0x0002  0x0001  0x0000
0b11010  0x0001  0x0002  0x0000
0b11010  0x0002  0x0002  0xFFFF
0b11010  0x0002  0x0000  0x0000
0b11010  0x0000  0x0002  0x0000
0b11010  0x0003  0x0002  0x0000

# greater than or equals
0b11011  0x0000  0x0000  0xFFFF
0b11011  0x0000  0x0001  0x0000
0b11011  0x0001  0x0000  0xFFFF
0b11011  0x0001  0x0001  0xFFFF
0b11011  0x0002  0x0001  0xFFFF
0b11011  0x0001  0x0002  0x0000
0b11011  0x0002  0x0002  0xFFFF
0b11011  0x0002  0x0000  0xFFFF
0b11011  0x0000  0x0002  0x0000
0b11011  0x0003  0x0002  0xFFFF

# less than
0b11100  0x0000  0x0000  0x0000
0b11100  0x0000  0x0001  0xFFFF
0b11100  0x0001  0x0000  0x0000
0b11100  0x0001  0x0001  0x0000
0b11100  0x0002  0x0001  0x0000
0b11100  0x0001  0x0002  0xFFFF
0b11100  0x0002  0x0002  0x0000
0b11100  0x0002  0x0000  0x0000
0b11100  0x0000  0x0002  0xFFFF
0b11100  0x0003  0x0002  0x0000

# less than or equals
0b11110  0x0000  0x0000  0xFFFF
0b11110  0x0000  0x0001  0xFFFF
0b11110  0x0001  0x0000  0x0000
0b11110  0x0001  0x0001  0xFFFF
0b11110  0x0002  0x0001  0x0000
0b11110  0x0001  0x0002  0xFFFF
0b11110  0x0002  0x0002  0xFFFF
0b11110  0x0002  0x0000  0x0000
0b11110  0x0000  0x0002  0xFFFF
0b11110  0x0003  0x0002  0x0000

# not equals
0b11101  0x0000  0x0000  0x0000
0b11101  0x0000  0x0001  0xFFFF
0b11101  0x0001  0x0000  0xFFFF
0b11101  0x0001  0x0001  0x0000
0b11101  0x0002  0x0001  0xFFFF
0b11101  0x0001  0x0002  0xFFFF
0b11101  0x0002  0x0002  0x0000
0b11101  0x0002  0x0000  0xFFFF
0b11101  0x0000  0x0002  0xFFFF
0b11101  0x0003  0x0002  0xFFFF

# true
0b11111  0x0000  0x0000  0xFFFF
0b11111  0x0000  0x0001  0xFFFF
0b11111  0x0001  0x0000  0xFFFF
0b11111  0x0001  0x0001  0xFFFF
0b11111  0x0002  0x0001  0xFFFF
0b11111  0x0001  0x0002  0xFFFF
0b11111  0x0002  0x0002  0xFFFF
0b11111  0x0002  0x0000  0xFFFF
0b11111  0x0000  0x0002  0xFFFF
0b11111  0x0003  0x0002  0xFFFF
*/
