// Digital circuit computer_foxbay.dig as structural Verilog
module computer_foxbay (
  input  programClock,
  input  [15:0] At_2,
  output [15:0] At
);

  wire and_1_out, and_2_out, and_4_out, and_5_out, and_6_out, \break , break_p1, break_p2, button_1_out,
       clock, comparator_1_gt, comparator_2_lt, device_oe, enable_dev, enable_dev_btn, enable_dev_fbswitch,
       enable_dev_midi, enable_gram, enable_ram, enable_rom, midi_C1, midi_C2, midi_C3, midi_C4, midi_C5,
       midi_C6, midi_C7, midi_C8, midi_OnOff, midi_PC, not_1_out, or_2_out, or_3_out, ram_oe, rom_oe,
       rs_ff_as_1_q, rs_ff_as_2_q, run_clock_out, step_out, video_oe, write_bus;
  wire [0:0] register_3_q;
  wire [1:0] enable_d;
  wire [2:0] device_enablement_d;
  wire [6:0] midi_N, midi_V;
  wire [7:0] D_out;
  wire [15:0] addr, addr_dec, addr_dec_internal, device_offset_d, in_proc, instruction, mask_d, out_dev,
       out_gram, out_ram, out_rom, ptr_inst, ramdualport_1_d, register_1_q, register_2_q, register_4_q,
       register_5_q, sub_1_s;

  Button step (.out(step_out));
  DipSwitch #(.dipDefault("true")) run_clock (.out(run_clock_out));
  // ButtonLED break: pin names not known; wires that end beside it: break_p1, break_p2
  Button LEFT (.out(D_out[5]));
  Button UP (.out(D_out[7]));
  Button DOWN (.out(D_out[6]));
  and and_1 (and_1_out, programClock, run_clock_out, ~break_p2);  // And
  D_FF_AS d_ff_as_1 (.Set(1'b0), .D(\break ), .C(clock), .Clr(break_p1), .Q(break_p2));  // open: nQ
  Button RIGHT (.out(D_out[4]));
  or or_1 (clock, step_out, and_1_out);
  Button A (.out(D_out[2]));
  Button W (.out(D_out[3]));
  Button D (.out(D_out[1]));
  Button S (.out(D_out[0]));
  assign out_dev = enable_dev_btn ? {{8{1'b0}}, D_out} : 16'bz;  // Driver driver_1
  RAMDualAccess #(.AddrBits(16), .Bits(16)) ramdualaccess_1 (
    .str(write_bus), .C(clock), .ld(1'b1), .A1(addr), .Din1({midi_PC, midi_OnOff, midi_V, midi_N}),
    .A2(At_2), .D2(At));  // open: D1
  or or_2 (or_2_out, ptr_inst[14], ptr_inst[15]);
  and and_2 (and_2_out, enable_dev_midi, write_bus);
  // Probe PC on ptr_inst[13:0]
  ROMDualPort #(.bigEndian("true"), .AddrBits(14), .isProgramMemory("true"), .Bits(16)) \program  (
    .A1(ptr_inst[13:0]), .s1(1'b1), .A2(addr_dec[13:0]), .s2(enable_rom), .D1(instruction), .D2(out_rom));
  Seven_Seg_Hex seven_seg_hex_1 (.d(At[15:12]), .dp(1'b0));
  Comparator #(.Bits(16)) comparator_1 (.a(At), .b(16'h200), .gt(comparator_1_gt));  // open: eq, lt
  Comparator #(.Bits(16)) comparator_2 (.a(At), .b(16'h100), .lt(comparator_2_lt));  // open: gt, eq
  // Probe I on instruction
  RS_FF_AS rs_ff_as_1 (.S(or_2_out), .R(1'b0), .Q(rs_ff_as_1_q));  // open: nQ
  ROM #(.AddrBits(3), .Bits(2)) enable (.A(addr[15:13]), .sel(1'b1), .D(enable_d));
  ROM #(.AddrBits(3), .Bits(16)) mask (.A(addr[15:13]), .sel(1'b1), .D(mask_d));
  ROM #(.AddrBits(3), .Bits(16)) device_offset (.A(addr_dec_internal[2:0]), .sel(1'b1), .D(device_offset_d));
  ROM #(.AddrBits(3), .Bits(3)) device_enablement (.A(addr_dec_internal[2:0]), .sel(1'b1), .D(device_enablement_d));
  Demultiplexer #(.Selector_Bits(3)) demultiplexer_1 (
    .sel(addr_dec[2:0]), .in(and_2_out), .out_0(midi_C1), .out_1(midi_C2), .out_2(midi_C3), .out_3(midi_C4),
    .out_4(midi_C5), .out_5(midi_C6), .out_6(midi_C7), .out_7(midi_C8));
  Seven_Seg_Hex seven_seg_hex_2 (.d(At[11:8]), .dp(1'b0));
  LED overflow (.in(rs_ff_as_1_q));
  Break break_2 (.brk(rs_ff_as_1_q));
  Decoder #(.Selector_Bits(2)) decoder_1 (
    .sel(enable_d), .out_0(enable_ram), .out_1(enable_gram), .out_2(enable_dev), .out_3(enable_rom));
  assign addr_dec_internal = mask_d & addr;  // And and_3, 16 bits wide
  Demultiplexer #(.Selector_Bits(3)) demultiplexer_2 (
    .sel(device_enablement_d), .in(enable_dev), .out_0(enable_dev_btn), .out_1(enable_dev_fbswitch),
    .out_2(enable_dev_midi));  // open: out_3, out_4, out_5, out_6, out_7
  Seven_Seg_Hex seven_seg_hex_3 (.d(At[7:4]), .dp(1'b0));
  or or_3 (or_3_out, comparator_1_gt, comparator_2_lt);
  Sub #(.Bits(16)) sub_1 (.a(addr_dec_internal), .b(device_offset_d), .c_i(1'b0), .s(sub_1_s));  // open: c_o
  Seven_Seg_Hex seven_seg_hex_4 (.d(At[3:0]), .dp(1'b0));
  Button button_1 (.out(button_1_out));
  Break break_3 (.brk(or_3_out));
  RS_FF_AS rs_ff_as_2 (.S(or_3_out), .R(button_1_out), .Q(rs_ff_as_2_q));  // open: nQ
  // MIDI #(.midiProgChange("true"), .midiInstrument("Violin")) C1: pin names not known; wires that end beside it: midi_N, midi_V, midi_OnOff, midi_PC, midi_C1, clock
  // MIDI #(.midiProgChange("true"), .midiInstrument("Violin")) C3: pin names not known; wires that end beside it: midi_N, midi_V, midi_OnOff, midi_PC, midi_C3, clock
  // MIDI #(.midiProgChange("true"), .midiInstrument("Violin")) C5: pin names not known; wires that end beside it: midi_N, midi_V, midi_OnOff, midi_PC, midi_C5, clock
  // MIDI #(.midiProgChange("true"), .midiInstrument("Violin")) C7: pin names not known; wires that end beside it: midi_N, midi_V, midi_OnOff, midi_PC, midi_C7, clock
  LED stack_corrupted (.in(rs_ff_as_2_q));
  cpu_proc16b1 cpu_proc16b1_1 (
    .inst(instruction), .bus_in(in_proc), .clock(clock), .ptr_inst(ptr_inst), .bus_addr(addr),
    .bus_out({midi_PC, midi_OnOff, midi_V, midi_N}), .bus_write(write_bus), .\break (\break ));
  // Probe addr on addr
  // Probe on addr
  // Probe on addr
  // Probe out_proc on {midi_PC, midi_OnOff, midi_V, midi_N}
  // Probe on {midi_PC, midi_OnOff, midi_V, midi_N}
  // Probe on {midi_PC, midi_OnOff, midi_V, midi_N}
  bus_driver ram (
    .oaddr(addr_dec), .oe(ram_oe), .oout(in_proc), .iaddr(addr_dec_internal), .ie(enable_ram), .iout(out_ram));
  bus_driver video (
    .oaddr(addr_dec), .oe(video_oe), .oout(in_proc), .iaddr(addr_dec_internal), .ie(enable_gram),
    .iout(out_gram));
  bus_driver rom (
    .oaddr(addr_dec), .oe(rom_oe), .oout(in_proc), .iaddr(addr_dec_internal), .ie(enable_rom), .iout(out_rom));
  bus_driver device (
    .oaddr(addr_dec), .oe(device_oe), .oout(in_proc), .iaddr(sub_1_s), .ie(enable_dev), .iout(out_dev));
  // MIDI #(.midiProgChange("true"), .midiInstrument("Violin")) C2: pin names not known; wires that end beside it: midi_N, midi_V, midi_OnOff, midi_PC, midi_C2, clock
  // MIDI #(.midiProgChange("true"), .midiInstrument("Violin")) C4: pin names not known; wires that end beside it: midi_N, midi_V, midi_OnOff, midi_PC, midi_C4, clock
  // MIDI #(.midiProgChange("true"), .midiInstrument("Violin")) C6: pin names not known; wires that end beside it: midi_N, midi_V, midi_OnOff, midi_PC, midi_C6, clock
  // MIDI #(.midiProgChange("true"), .midiInstrument("Violin")) C8: pin names not known; wires that end beside it: midi_N, midi_V, midi_OnOff, midi_PC, midi_C8, clock
  LED led_1 (.in(ram_oe));
  LED led_2 (.in(video_oe));
  LED led_3 (.in(rom_oe));
  LED led_4 (.in(device_oe));
  // Probe on write_bus
  Register #(.Bits(16)) register_1 (.D(ptr_inst), .C(clock), .en(1'b1), .Q(register_1_q));
  and and_4 (and_4_out, enable_ram, write_bus);
  and and_5 (and_5_out, enable_dev_fbswitch, write_bus);
  Register #(.Bits(16)) register_2 (.D(register_1_q), .C(clock), .en(1'b1), .Q(register_2_q));
  // Probe latest on register_1_q
  and and_6 (and_6_out, enable_gram, write_bus);
  not not_1 (not_1_out, write_bus);
  // Probe on register_2_q
  Register register_3 (.D(midi_N[0]), .C(clock), .en(and_5_out), .Q(register_3_q[0]));
  Register #(.Bits(16)) register_4 (.D(register_2_q), .C(clock), .en(1'b1), .Q(register_4_q));
  RAMDualPort #(.AddrBits(14), .Bits(16)) ramdualport_1 (
    .A(addr_dec[13:0]), .Din({midi_PC, midi_OnOff, midi_V, midi_N}), .str(and_4_out), .C(clock), .ld(1'b1),
    .D(ramdualport_1_d));
  GraphicCard #(.graphicHeight(64), .graphicWidth(96), .Bits(16)) graphiccard_1 (
    .A(addr_dec[13:0]), .str(and_6_out), .C(clock), .ld(not_1_out), .B(register_3_q[0]), .D(out_gram));
  Register #(.Bits(16)) register_5 (.D(register_4_q), .C(clock), .en(1'b1), .Q(register_5_q));
  // Probe on register_4_q
  assign out_ram = enable_ram ? ramdualport_1_d : 16'bz;  // Driver driver_2
  assign out_gram = and_6_out ? {midi_PC, midi_OnOff, midi_V, midi_N} : 16'bz;  // Driver driver_3
  assign out_dev = enable_dev_fbswitch ? {{15{1'b0}}, register_3_q[0]} : 16'bz;  // Driver driver_4
  // Probe on register_5_q

  // Other names for the same wires on the sheet: out_proc[15:0] = {midi_PC, midi_OnOff, midi_V, midi_N}

  // Notes on the sheet:
  //   programClock: Hz: 150000
  //   clock
  //   button device
  //   bits 15-8 are 0
  //   7 6543210
  //   UDLRAZSX
  //   TODO: program tests
  //   Address map:
  //   0b00 0x0000 - 0x3FFF (16Ki) RAM
  //   0b01 0x4000 - 0x7FFF (16Ki) video memory
  //   0b10 0x8000 - 0xBFFF (16Ki) devices
  //   0b11 0xC000 - 0xFFFF (16Ki) instruction ROM
  //   devices:
  //   0x0000: button inputs
  //   0x0001: framebuffer switch
  //   0x0002 - 0x000A: midi channel 1-8
  //   address bus test instrumentation
  //   program memory
  //   bus controller
  //   midi device v2
  //   map region selector
  //   device selector
  //   06-00: N
  //   13-07: V
  //   14: OnOff
  //   15: program change
  //   program loads pong.out
  //   contents of enable (hex, n*v repeats v):
  //   0,0,1,1,2,2,3,3
  //   contents of mask (hex, n*v repeats v):
  //   8*3fff
  //   contents of device_offset (hex, n*v repeats v):
  //   0,1,2,2,4*4
  //   contents of device_enablement (hex, n*v repeats v):
  //   0,1,2,2,4*4
  //   cpu
  //   instruction pointer history
  //   RAM
  //   graphic RAM + fbswitch device
  //   fbswitch device:
  //   bit 0 is a 1-bit register that
  //   controls the active framebuffer
  //   all other bits are unconnected
endmodule
