// Digital circuit operand_selector.dig as structural Verilog
module operand_selector (
  input  [15:0] reg_A,
  input  [15:0] reg_B,
  input  [15:0] reg_C,
  input  [15:0] reg_D,
  input  [15:0] reg_rem,
  input  [15:0] reg_flags,
  input  [15:0] jump,
  input  [15:0] PC,
  input  [15:0] ALU,
  input  [15:0] bus,
  input  [15:0] constant
);

  value_selector value_selector_1 (
    .reg_A(reg_A), .reg_B(reg_B), .reg_C(reg_C), .reg_D(reg_D), .reg_rem(reg_rem), .reg_flags(reg_flags),
    .jump(jump), .PC(PC), .ALU(ALU), .bus(bus), .constant(constant));  // open: sel, val
endmodule
