// Digital circuit decoder.dig as structural Verilog
module decoder (
  input  [15:0] instruction,
  output [2:0] mode,
  output [15:0] arg0,
  output [15:0] arg1,
  output [15:0] arg2,
  output [15:0] arg3
);

  wire and_1_out, and_2_out, and_3_out, and_4_out, and_5_out, not_1_out, not_2_out;
  wire [2:0] priorityencoder_1_num;
  wire [15:0] brk_arg0, brk_arg1, brk_arg2, brk_arg3, bus_arg0, bus_arg1, bus_arg2, bus_arg3, jump_arg0,
       jump_arg1, jump_arg2, jump_arg3, lde_arg0, lde_arg1, lde_arg2, lde_arg3, mov_arg2, mov_arg3;
  wire [15:3] alu_arg0, alu_arg1, ldc_arg0, mov_arg0;
  wire [15:4] alu_arg2, alu_arg3;
  wire [15:9] mov_arg1;
  wire [15:12] ldc_arg1;

  and and_1 (and_1_out, instruction[10], ~instruction[11]);  // And
  and and_2 (and_2_out, ~instruction[10], ~instruction[11]);  // And
  and and_3 (and_3_out, ~instruction[12], instruction[13]);  // And
  and and_4 (and_4_out, instruction[12], ~instruction[13]);  // And
  and and_5 (and_5_out, ~instruction[12], ~instruction[13]);  // And
  not not_1 (not_1_out, instruction[14]);
  not not_2 (not_2_out, instruction[15]);
  PriorityEncoder #(.Selector_Bits(3)) priorityencoder_1 (
    .in0(1'b1), .in1(and_1_out), .in2(and_2_out), .in3(and_3_out), .in4(and_4_out), .in5(and_5_out),
    .in6(not_1_out), .in7(not_2_out), .num(priorityencoder_1_num));  // open: any
  assign mode = ~priorityencoder_1_num;  // Not not_3, 3 bits wide
  Multiplexer #(.Bits(16), .Selector_Bits(3)) multiplexer_1 (
    .sel(mode), .in_0({ldc_arg0, instruction[14:12]}), .in_1({alu_arg0, instruction[13:11]}),
    .in_2({mov_arg0, instruction[11:9]}), .in_3(bus_arg0), .in_4(jump_arg0), .in_5(brk_arg0),
    .in_6(lde_arg0), .in_7({16{1'b0}}), .out(arg0));
  Multiplexer #(.Selector_Bits(3), .Bits(16)) multiplexer_2 (
    .sel(mode), .in_0({ldc_arg1, instruction[11:0]}), .in_1({alu_arg1, instruction[10:8]}),
    .in_2({mov_arg1, instruction[8:0]}), .in_3(bus_arg1), .in_4(jump_arg1), .in_5(brk_arg1), .in_6(lde_arg1),
    .in_7({16{1'b0}}), .out(arg1));
  Multiplexer #(.Selector_Bits(3), .Bits(16)) multiplexer_3 (
    .sel(mode), .in_0({16{1'b0}}), .in_1({alu_arg2, instruction[7:4]}), .in_2(mov_arg2), .in_3(bus_arg2),
    .in_4(jump_arg2), .in_5(brk_arg2), .in_6(lde_arg2), .in_7({16{1'b0}}), .out(arg2));
  Multiplexer #(.Selector_Bits(3), .Bits(16)) multiplexer_4 (
    .sel(mode), .in_0({16{1'b0}}), .in_1({alu_arg3, instruction[3:0]}), .in_2(mov_arg3), .in_3(bus_arg3),
    .in_4(jump_arg3), .in_5(brk_arg3), .in_6(lde_arg3), .in_7({16{1'b0}}), .out(arg3));
  // Pins of 3 and 16 bits meet at {ldc_arg0, instruction[14:12]}
  // Pins of 3 and 16 bits meet at {alu_arg0, instruction[13:11]}
  // Pins of 3 and 16 bits meet at {mov_arg0, instruction[11:9]}
  // Pins of 12 and 16 bits meet at {ldc_arg1, instruction[11:0]}
  // Pins of 3 and 16 bits meet at {alu_arg1, instruction[10:8]}
  // Pins of 9 and 16 bits meet at {mov_arg1, instruction[8:0]}
  // Pins of 4 and 16 bits meet at {alu_arg2, instruction[7:4]}
  // Pins of 4 and 16 bits meet at {alu_arg3, instruction[3:0]}

  // Other names for the same wires on the sheet: alu_arg3[3:0] = instruction[3:0]; ldc_arg1[11:0] = instruction[11:0];
  //   mov_arg1[8:0] = instruction[8:0]; alu_arg2[3:0] = instruction[7:4]; alu_arg1[2:0] = instruction[10:8];
  //   mov_arg0[2:0] = instruction[11:9]; alu_arg0[2:0] = instruction[13:11]; ldc_arg0[2:0] = instruction[14:12]

  // Notes on the sheet:
  //   ldc
  //   alu
  //   mov
  //   bus
  //   mode:
  //   000: ldc
  //   001: alu
  //   010: mov
  //   011: bus
  //   100: jump
  //   101: noop/break
  //   110: lde
  //   111: unassigned
  //   ldc:
  //   arg0: write register
  //   arg1: constant unsigned 14
  //   alu
  //   arg0: write register
  //   arg1: lhs register
  //   arg2: rhs 4-bit
  //   arg3: opcode
  //   mov
  //   arg0: write register
  //   arg1: read register 9
  //   bus:
  //   arg0: load (0) store (1)
  //   arg1: address register
  //   arg2: value 8-bit
  //   jump:
  //   arg0: condition (see doc)
  //   arg1: comparand register
  //   arg2: jump target 7-bit
  //   noop/break
  //   arg0: brk pin value 1
  //   arg1: address 9-bit
  //   lde:
  //   arg0: write register
  //   arg1: constant unsigned 4
endmodule

/* Test case mode tests:
instruction         mode
# ldc
0b0000000000000000  0b000
0b0100000000000000  0b000
0b0110000000000000  0b000

# alu
0b1000000000000000  0b001
0b1010000000000000  0b001

# mov
0b1100000000000000  0b010
0b1100100000000000  0b010

# bus
0b1101000000000000  0b011
0b1101100000000000  0b011

# jump
0b1110000000000000  0b100
0b1110100000000000  0b100

# noop/break
0b1111000000000000  0b101
0b1111001000000000  0b101

# lde
0b1111010000000000  0b110
0b1111011000000000  0b110

# unassigned
0b1111100000000000  0b111
0b1111101000000000  0b111
0b1111110000000000  0b111
0b1111111000000000  0b111
*/
