// Digital circuit cpu_proc16b1.dig as structural Verilog
module cpu_proc16b1 (
  input  [15:0] instruction,
  input  [15:0] bus_in,
  input  clock
);

  wire and_1_out, and_2_out, and_3_out, and_4_out, and_5_out, jump_success, mode_alu, mode_break,
       mode_constant, mode_jump, mode_noop, mode_readwrite, read_a, read_b, read_bus, read_c, read_d, read_o,
       read_r, write_a, write_b, write_bus, write_c, write_d, write_enable, write_overflow;
  wire [1:0] alu_x, alu_y, jump_tgt, jump_x, jump_y;
  wire [2:0] bus_address_sel, decoder_1_mode, jump_cmp;
  wire [4:0] alu_op;
  wire [15:0] add_1_s, alu_1_z, alu_operands_1_x, alu_operands_1_y, alu_operands_2_x, alu_operands_2_y,
       constant_value, multiplexer_1_out, reg_a, reg_b, reg_c, reg_d, reg_o, reg_pc, reg_r, write_pc,
       write_remainder, write_val;

  and and_1 (and_1_out, write_a, write_enable);
  and and_2 (and_2_out, write_b, write_enable);
  and and_3 (and_3_out, write_c, write_enable);
  and and_4 (and_4_out, write_d, write_enable);
  decoder decoder_1 (
    .instruction(instruction), .mode(decoder_1_mode), .constant_value(constant_value), .alu_x(alu_x),
    .alu_y(alu_y), .alu_op(alu_op), .jump_x(jump_x), .jump_y(jump_y), .jump_tgt(jump_tgt),
    .jump_cmp(jump_cmp), .bus_address(bus_address_sel), .read_a(read_a), .read_b(read_b), .read_c(read_c),
    .read_d(read_d), .read_bus(read_bus), .read_o(read_o), .read_r(read_r), .write_enable(write_enable),
    .write_a(write_a), .write_b(write_b), .write_c(write_c), .write_d(write_d), .write_bus(write_bus));
  Register #(.Bits(16)) A (.D(write_val), .C(clock), .en(and_1_out), .Q(reg_a));
  Register #(.Bits(16)) B (.D(write_val), .C(clock), .en(and_2_out), .Q(reg_b));
  Register #(.Bits(16)) C (.D(write_val), .C(clock), .en(and_3_out), .Q(reg_c));
  Register #(.Bits(16)) D (.D(write_val), .C(clock), .en(and_4_out), .Q(reg_d));
  Register #(.Bits(16)) o (.D({{15{1'b0}}, write_overflow}), .C(clock), .en(mode_alu), .Q(reg_o));
  Register #(.Bits(16)) r (.D(write_remainder), .C(clock), .en(mode_alu), .Q(reg_r));
  Register #(.Bits(16)) PC (.D(write_pc), .C(clock), .en(1'b1), .Q(reg_pc));
  // Probe reg_a on reg_a
  // Probe reg_b on reg_b
  // Probe reg_c on reg_c
  // Probe reg_d on reg_d
  // Probe reg_o on reg_o
  // Probe reg_r on reg_r
  // Probe reg_pc on reg_pc
  Demultiplexer #(.Selector_Bits(3)) demultiplexer_1 (
    .sel(decoder_1_mode), .in(1'b1), .out_0(mode_constant), .out_1(mode_alu), .out_2(mode_jump),
    .out_3(mode_readwrite), .out_4(mode_noop), .out_5(mode_break));  // open: out_6, out_7
  assign write_val = mode_constant ? constant_value : 16'bz;  // Driver driver_1
  Multiplexer #(.Selector_Bits(2), .Bits(16)) multiplexer_1 (
    .sel(jump_tgt), .in_0(reg_a), .in_1(reg_b), .in_2(reg_c), .in_3(reg_d), .out(multiplexer_1_out));
  alu_operands alu_operands_1 (
    .Xsel(jump_x), .Ysel(jump_y), .a(reg_a), .b(reg_b), .c(reg_c), .d(reg_d), .X(alu_operands_1_x),
    .Y(alu_operands_1_y));
  Add #(.Bits(16)) add_1 (.a(reg_pc), .b(16'h1), .c_i(1'b0), .s(add_1_s));  // open: c_o
  and and_5 (and_5_out, mode_jump, jump_success);
  Multiplexer #(.Bits(16)) multiplexer_2 (.sel(and_5_out), .in_0(add_1_s), .in_1(multiplexer_1_out), .out(write_pc));
  // compare compare_1: pin names not known; wires that end beside it: alu_operands_1_x, alu_operands_1_y, jump_cmp, jump_success
  alu_operands alu_operands_2 (
    .Xsel(alu_x), .Ysel(alu_y), .a(reg_a), .b(reg_b), .c(reg_c), .d(reg_d), .X(alu_operands_2_x),
    .Y(alu_operands_2_y));
  alu alu_1 (
    .opcode(alu_op), .X(alu_operands_2_x), .Y(alu_operands_2_y), .Z(alu_1_z), .remainder(write_remainder),
    .overflow(write_overflow));
  assign write_val = mode_alu ? alu_1_z : 16'bz;  // Driver driver_2

  // Notes on the sheet:
  //   input/decoder
  //   registers
  //   program counter manager
  //   jump
  //   alu
endmodule

/* Test case ldc tests:
clock instruction  bus_in  reg_a  reg_b  reg_c  reg_d  reg_o  reg_r
C  0b0000000000000001  0   1  0  0  0  0  0
C  0b0000000000000010  0   2  0  0  0  0  0
C  0b0001000000000011  0   2  3  0  0  0  0
C  0b0010000000000100  0   2  3  4  0  0  0
C  0b0011000000000101  0   2  3  4  5  0  0
*/

/* Test case alu tests:
clock instruction  reg_a  reg_b  reg_c  reg_d  reg_r
# ldc %a, $1
C  0b0000000000000001  1  0  0  0  x
# ldc %b, $2
C  0b0001000000000010  1  2  0  0  x

# add %c, %a, %b
#    01xxyywwooooo___
C  0b0100011000000000  1  2  3  0  x

# sub %c, %b, %a
C  0b0101001000001000  1  2  1  0  x

# div %c, %a, %b
C  0b0100011000011000  1  2  0  0  1
*/

/* Test case jump tests:
clock  instruction  reg_a  reg_b  reg_c  reg_d  reg_pc
# ldc %a, $1
#    00rrvvvvvvvvvvvv
C  0b0000000000000001  1  0  0  0  1

# ldc %b, $2
C  0b0001000000000010  1  2  0  0  2

# ldc %d, $0xFF
C  0b0011000011111111  1  2  0  0xFF 3

# jgt %c, %a, %b (jump to c if a > b) (it's not)
#    100xxyyttccc____
C  0b1000001100010000  1  2  0  0xFF  4

# jlt %c, %a, %b (jump to c if a < b) (it is)
#    100xxyyttccc____
C  0b1000001100010000  1  2  0  0xFF  0

# jlt %d, %a, %b (jump to d if a < b) (it is)
#    100xxyyttccc____
C  0b1000001100010000  1  2  0  0xFF  0xFF

# jump to c if false
#    100xxyyttccc____
C  0b1000001100000000  1  2  0  0xFF  0x100

# jmp %c (jump to c if true)
#    100xxyyttccc____
C  0b1000001101110000  1  2  0  0xFF  0
*/
