// Digital circuit decode16a1.dig as structural Verilog
module decode16a1 (
  input  [15:0] I,
  output [4:0] ALU,
  output [1:0] ALU_A,
  output [1:0] ALU_B,
  output [1:0] D_sel,
  output Ax,
  output B,
  output A,
  output [2:0] cmp,
  output brk,
  output cmp_o,
  output Ax_sel,
  output jmp,
  output ALU_rsel
);

  wire [11:10] multiplexer_1_out;
  wire [20:0] multiplexer_2_out, multiplexer_3_out, multiplexer_4_out;

  Multiplexer #(.Bits(2)) multiplexer_1 (.sel(I[3]), .in_0(2'b11), .in_1(2'b10), .out(multiplexer_1_out));
  Multiplexer #(.Bits(21)) multiplexer_2 (
    .sel(I[0]), .in_0({21{1'b0}}), .in_1({I[0], {20{1'b0}}}), .out(multiplexer_2_out));
  Multiplexer #(.Bits(21)) multiplexer_3 (
    .sel(I[11]), .in_0({2'b01, I[3:0], 3'b000, multiplexer_1_out, {10{1'b0}}}), .in_1(multiplexer_2_out),
    .out(multiplexer_3_out));
  Multiplexer #(.Bits(21)) multiplexer_4 (
    .sel(I[13]), .in_0({{6{1'b0}}, I[0], I[1], I[2], 2'b01, I[9:8], I[11:10], I[7:3], I[12]}),
    .in_1(multiplexer_3_out), .out(multiplexer_4_out));
  Multiplexer #(.Bits(21)) multiplexer_5 (
    .sel(I[15]), .in_0(21'h4000), .in_1(multiplexer_4_out),
    .out({brk, jmp, cmp_o, cmp, A, B, Ax, D_sel, ALU_B, ALU_A, ALU, ALU_rsel}));

  assign Ax_sel = I[14];

  // Notes on the sheet:
  //   cmp: opcode for compare component
  //   data word decode
  //   ALU decode
  //   jump decode
  //   break decode
endmodule

/* Test case decode test:
I                   ALU_rsel Ax_sel ALU      ALU_A ALU_B D_sel Ax B A cmp   cmp_o jmp brk

# data words
0x0000              0        0      0b00000  0b00  0b00  0b00  0  0 1 0b000 0     0   0
0x0001              0        0      0b00000  0b00  0b00  0b00  0  0 1 0b000 0     0   0
0x0002              0        0      0b00000  0b00  0b00  0b00  0  0 1 0b000 0     0   0
0x0030              0        0      0b00000  0b00  0b00  0b00  0  0 1 0b000 0     0   0

# alu
# aluRXsYsAluop*BA
0b1000101000000001  0        0      0b00000  0b10  0b10  0b01  0  0 1 0b000 0     0   0
0b1001001000000010  1        0      0b00000  0b00  0b10  0b01  0  1 0 0b000 0     0   0
0b1101001000000010  1        1      0b00000  0b00  0b10  0b01  0  1 0 0b000 0     0   0
0b1000110110110110  0        0      0b10110  0b11  0b01  0b01  1  1 0 0b000 0     0   0

# jump
0b1010000000001111  0        0      0b00000  0b00  0b00  0b10  0  0 0 0b111 1     1   0
0b1010000000001001  0        0      0b00000  0b00  0b00  0b10  0  0 0 0b001 1     1   0
0b1010000000000100  0        0      0b00000  0b00  0b00  0b11  0  0 0 0b100 0     1   0

# break
0b1010100000000000  0        0      0b00000  0b00  0b00  0b00  0  0 0 0b000 0     0   0
0b1010100000000001  0        0      0b00000  0b00  0b00  0b00  0  0 0 0b000 0     0   1
*/
