// Digital circuit proc16a1.dig as structural Verilog
module proc16a1 (
  input  program_clock
);

  wire and_1_out, compare16_1_1_r, or_1_out, or_2_out, or_3_out, or_4_out, reset_PC_out, rs_ff_as_1_q,
       start_clock_out, step_out, stop_clock_out;
  wire [2:0] demultiplexer_3_out_0_2;
  wire [7:0] demultiplexer_3_out_0;
  wire [10:0] demultiplexer_3_out_1;
  wire [11:0] demultiplexer_2_out_0, demultiplexer_2_out_1;
  wire [14:0] demultiplexer_1_out_0, demultiplexer_1_out_1;
  wire [15:0] A_register_q, ALU_r, B_register_q, multiplexer_1_out, multiplexer_2_out, multiplexer_3_out,
       Program_counter_out, RAM_d, rom_1_d;

  RS_FF_AS rs_ff_as_1 (.S(start_clock_out), .R(or_1_out), .Q(rs_ff_as_1_q));  // open: nQ
  Button start_clock (.out(start_clock_out));
  Button stop_clock (.out(stop_clock_out));
  or or_1 (or_1_out, stop_clock_out, demultiplexer_3_out_1[0]);
  and and_1 (and_1_out, program_clock, rs_ff_as_1_q);
  Button step (.out(step_out));
  Button reset_PC (.out(reset_PC_out));
  or or_2 (or_2_out, and_1_out, or_3_out);
  or or_3 (or_3_out, step_out, reset_PC_out);
  CounterPreset #(.maxValue(65535), .Bits(16), .isProgramCounter("true")) Program_counter (
    .en(1'b1), .C(or_2_out), .dir(1'b0), .in(multiplexer_3_out), .ld(compare16_1_1_r), .clr(reset_PC_out),
    .out(Program_counter_out));  // open: ovf
  Register #(.Bits(16)) A_register (.D(multiplexer_3_out), .C(or_2_out), .en(or_4_out), .Q(A_register_q));
  Register #(.Bits(16)) B_register (
    .D(multiplexer_3_out), .C(or_2_out), .en(demultiplexer_2_out_0[1]), .Q(B_register_q));
  RAMDualPort #(.AddrBits(16), .Bits(16)) RAM (
    .A(multiplexer_1_out), .Din(multiplexer_3_out), .str(demultiplexer_2_out_0[2]), .C(or_2_out), .ld(1'b1),
    .D(RAM_d));
  ROM #(.AddrBits(16), .isProgramMemory("true"), .Bits(16)) rom_1 (.A(Program_counter_out), .sel(1'b1), .D(rom_1_d));
  Multiplexer #(.Bits(16)) multiplexer_1 (
    .sel(demultiplexer_1_out_1[14]), .in_0(A_register_q), .in_1(B_register_q), .out(multiplexer_1_out));
  // Probe on multiplexer_1_out
  // Probe on Program_counter_out
  // Probe on rom_1_d
  // Probe on A_register_q
  // Probe on B_register_q
  // Probe on RAM_d
  Demultiplexer #(.Bits(15)) demultiplexer_1 (
    .sel(rom_1_d[15]), .in(rom_1_d[14:0]), .out_0(demultiplexer_1_out_0), .out_1(demultiplexer_1_out_1));
  or or_4 (or_4_out, demultiplexer_2_out_0[0], rom_1_d[15]);
  Demultiplexer #(.Bits(12)) demultiplexer_2 (
    .sel(demultiplexer_1_out_1[12]), .in(demultiplexer_1_out_1[11:0]), .out_0(demultiplexer_2_out_0),
    .out_1(demultiplexer_2_out_1));
  Demultiplexer #(.Bits(11)) demultiplexer_3 (
    .sel(demultiplexer_2_out_1[11]), .in(demultiplexer_2_out_1[10:0]),
    .out_0({demultiplexer_3_out_0_2, demultiplexer_3_out_0}), .out_1(demultiplexer_3_out_1));
  alu16_2 ALU (.opcode(demultiplexer_2_out_0), .A(A_register_q), .B(B_register_q), .Ax(RAM_d), .R(ALU_r));
  Multiplexer #(.Bits(16)) multiplexer_2 (
    .sel(demultiplexer_3_out_0[7]), .in_0(A_register_q), .in_1(B_register_q), .out(multiplexer_2_out));
  compare16_1 compare16_1_1 (.A(multiplexer_2_out), .B({16{1'b0}}), .m(demultiplexer_3_out_0_2), .r(compare16_1_1_r));
  Multiplexer #(.Bits(16)) multiplexer_3 (
    .sel(rom_1_d[15]), .in_0({1'b0, demultiplexer_1_out_0}), .in_1(ALU_r), .out(multiplexer_3_out));
  // Probe on multiplexer_3_out

  // Notes on the sheet:
  //   Clock
  //   contents of rom_1 (hex, n*v repeats v):
  //   0,1,2,3,8201,12,8201,8201
  //   data word instruction
  //   jump instruction
  //   break instruction
  //   ALU instruction
endmodule
